# Fritzing sketch CCU_PCB (saved by Fritzing 0.9.3b)
circuit board: 9.8cm x 5.60534cm
breadboards: 1

parts:
  CapSense2 = Adafruit AT42QT1010 Standalone Momentary Capacitive Touch Sensor [part_number="Adafruit #1374"]
  SolOUT1 = 3.5mm Audio Jack [package=audio-jack]
  DI1 = 3.5mm Audio Jack [package=audio-jack]
  Relay1 = Relay 2 x switch [part_number=351 package=THT]
  5V = 3.5mm Audio Jack [package=audio-jack]
  DO1 = 3.5mm Audio Jack [package=audio-jack]
  LIN2 = 3.5mm Audio Jack [package=audio-jack]
  D = Rectifier Diode [part_number=1N4001 package="300 mil [THT]"]
  R = Resistor [tolerance=±5% resistance=220 package=THT]
  12VIN = Power plug
  DO3 = BNC [package=bnc]
  LED1 = Screw terminal - 2 pins [package=THT]
  C1 = Electrolytic Capacitor [capacitance=1µF package="100 mil [THT, electrolytic]"]
  C = Electrolytic Capacitor [capacitance=1µF package="100 mil [THT, electrolytic]"]
  LIN1 = 3.5mm Audio Jack [package=audio-jack]
  SolOUT2 = 3.5mm Audio Jack [package=audio-jack]
  Relay2 = Relay 2 x switch [part_number=351 package=THT]
  D_2 = Rectifier Diode [part_number=1N4001 package="300 mil [THT]"]
  Switch5 = female pin header, 2 pins [form="♀ (female)"]
  Part1 = RPi hat - blank [part_number=RPI-blank]
  C_2 = Electrolytic Capacitor [capacitance=1µF package="100 mil [THT, electrolytic]"]
  Switch = female pin header, 3 pins [form="♀ (female)"]
  R_2 = Resistor [tolerance=±5% resistance=220 package=THT]
  CapSense1 = Adafruit AT42QT1010 Standalone Momentary Capacitive Touch Sensor [part_number="Adafruit #1374"]

nets:
  N1: CapSense2.LEDA, C.-, Part1.GND#37, C_2.-, CapSense1.LEDA
  N2: CapSense2.VDD, Part1.GPIO6, C_2.+
  N3: CapSense2.OUT, 5V.RIGHT, Part1.5.0V, CapSense1.OUT
  N4: SolOUT1.RIGHT, Relay1.pin_13, D.cathode
  N5: SolOUT1.LEFT, D.anode, 12VIN.GND, C1.-, SolOUT2.LEFT, D_2.anode
  N6: DI1.RIGHT, Part1.GND#12, Part1.GPIO17
  N7: DI1.LEFT, Relay1.pin_1, 5V.LEFT, DO1.LEFT, DO3.GND, LED1.pin2, Relay2.pin_1, Part1.GND#56, Part1.GND#61, Switch.pin1
  N8: Relay1.pin_9, 12VIN.VCC, C1.+, Relay2.pin_9
  N9: Relay1.pin_16, Part1.GPIO22
  N10: DO1.RIGHT, R.Pin_0
  N11: LIN2.SLEEVE, Switch5.pin1
  N12: R.Pin_1, Part1.GPIO24
  N13: DO3.OUT, R_2.Pin_1
  N14: LED1.pin1, Part1.3.3V#11, Part1.GPIO4, Switch.pin2
  N15: C.+, Part1.GPIO5, CapSense1.VDD
  N16: LIN1.SLEEVE, Switch5.pin2
  N17: SolOUT2.RIGHT, Relay2.pin_13, D_2.cathode
  N18: Relay2.pin_16, Part1.GPIO13
  N19: Part1.GPIO23, R_2.Pin_0
  N20: Part1.3.3V#48, Switch.pin3

custom parts:
  Adafruit AT42QT1010 Standalone Momentary Capacitive Touch Sensor: This breakout board is the simplest way to create a project with a single "momentary" capacitive touch sensor. No microcontroller is required here - just power with 1.8 to 5.5VDC and touch the pad to activate the sensor. When a capacitive load is detected (e.g. a person touches the sensor-pad area) the red LED lights up and the output pin goes high. You can also solder a wire to the middle pad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
  Relay 2 x switch: An DPDT relay. 2 x switch, same footprint as G5 V-2 Omron or V23042 Siemens
